// Logisim project stack_logical_normal.circ as structural Verilog: 17 circuits, main circuit main
module main (
  input  CLK,
  input  RESET,
  input  [1:0] COMMAND,
  input  [2:0] INDEX,
  input  [3:0] IO_DATA_in,
  output [3:0] IO_DATA_out
);

  wire [3:0] stack_1_d0, stack_1_d1, stack_1_d2, stack_1_d3, stack_1_d4;

  // Probe on stack_1_d0
  stack stack_1 (
    .CLK(CLK), .RESET(RESET), .COMMAND(COMMAND), .INDEX(INDEX), .IO_DATA_in(IO_DATA_in), .d0(stack_1_d0),
    .d1(stack_1_d1), .d2(stack_1_d2), .d3(stack_1_d3), .d4(stack_1_d4), .IO_DATA_out(IO_DATA_out));
  // Probe on stack_1_d1
  // Probe on stack_1_d2
  // Probe on stack_1_d3
  // Probe on stack_1_d4
endmodule

module stack (
  input  CLK,
  input  RESET,
  input  [1:0] COMMAND,
  input  [2:0] INDEX,
  input  [3:0] IO_DATA_in,
  output [3:0] d0,
  output [3:0] d1,
  output [3:0] d2,
  output [3:0] d3,
  output [3:0] d4,
  output [3:0] IO_DATA_out
);

  wire C, CLK0, CLK1, CLK2, CLK3, CLK4, f0, f1, f2, f3, f4, get, M0, M1, M2, nop, or_1_out, pop, push, Val0,
       Val1, Val2, Val3, WRITE;

  and and_1 (C, push, CLK);
  or or_1 (or_1_out, pop, get);
  and and_2 (WRITE, CLK, or_1_out);
  from3to5 from3to5_1 (
    .FIRSTBIN(M0), .SECONDBIN(M1), .THIRDBIN(M2), .VAL0(f0), .VAL1(f1), .VAL2(f2), .VAL3(f3), .VAL4(f4));
  Commands commands_1 (.BIT0(COMMAND[0]), .BIT1(COMMAND[1]), .nop(nop), .push(push), .pop(pop), .get(get));
  parseCommands parsecommands_1 (
    .Com0(COMMAND[0]), .Com1(COMMAND[1]), .Reset(RESET), .CLK(CLK), .IND0(INDEX[0]), .IND1(INDEX[1]),
    .IND2(INDEX[2]), .M0(M0), .M1(M1), .M2(M2));
  and and_3 (CLK0, C, f0);
  and and_4 (CLK1, C, f1);
  and and_5 (CLK2, C, f2);
  and and_6 (CLK3, C, f3);
  and and_7 (CLK4, C, f4);
  MEM mem_1 (
    .Reset(RESET), .CLK(C), .VAL0(IO_DATA_in[0]), .VAL1(IO_DATA_in[1]), .VAL2(IO_DATA_in[2]),
    .VAL3(IO_DATA_in[3]), .Ind0(M0), .Ind1(M1), .Ind2(M2), .O0(Val0), .O1(Val1), .O2(Val2), .O3(Val3));
  parser parser_1 (
    .FLAG(WRITE), .VAL0(Val0), .VAL1(Val1), .VAL2(Val2), .VAL3(Val3), .out_6(IO_DATA_in[0]),
    .out_7(IO_DATA_in[1]), .out_8(IO_DATA_in[2]), .out_9(IO_DATA_in[3]));
  BlockOfMemory blockofmemory_1 (
    .CLK(CLK0), .RESET(RESET), .VAL0(Val0), .VAL1(Val1), .VAL2(Val2), .VAL3(Val3), .Q0(d0[0]), .Q1(d0[1]),
    .Q2(d0[2]), .Q3(d0[3]));
  BlockOfMemory blockofmemory_2 (
    .CLK(CLK1), .RESET(RESET), .VAL0(Val0), .VAL1(Val1), .VAL2(Val2), .VAL3(Val3), .Q0(d1[0]), .Q1(d1[1]),
    .Q2(d1[2]), .Q3(d1[3]));
  BlockOfMemory blockofmemory_3 (
    .CLK(CLK2), .RESET(RESET), .VAL0(Val0), .VAL1(Val1), .VAL2(Val2), .VAL3(Val3), .Q0(d2[0]), .Q1(d2[1]),
    .Q2(d2[2]), .Q3(d2[3]));
  BlockOfMemory blockofmemory_4 (
    .CLK(CLK3), .RESET(RESET), .VAL0(Val0), .VAL1(Val1), .VAL2(Val2), .VAL3(Val3), .Q0(d3[0]), .Q1(d3[1]),
    .Q2(d3[2]), .Q3(d3[3]));
  BlockOfMemory blockofmemory_5 (
    .CLK(CLK4), .RESET(RESET), .VAL0(Val0), .VAL1(Val1), .VAL2(Val2), .VAL3(Val3), .Q0(d4[0]), .Q1(d4[1]),
    .Q2(d4[2]), .Q3(d4[3]));
  // Probe on IO_DATA_in[0]

  assign IO_DATA_out = IO_DATA_in;

  // Other names for the same wires on the sheet: COM0 = COMMAND[0]; COM1 = COMMAND[1]; IND0 = INDEX[0];
  //   IND1 = INDEX[1]; IND2 = INDEX[2]; InputBit0 = IO_DATA_in[0]; OutputBit0 = IO_DATA_in[0];
  //   InputBit1 = IO_DATA_in[1]; OutputBit1 = IO_DATA_in[1]; InputBit2 = IO_DATA_in[2]; OutputBit2 = IO_DATA_in[2];
  //   InputBit3 = IO_DATA_in[3]; OutputBit3 = IO_DATA_in[3]
endmodule

module parseCommands (
  input  Com0,
  input  Com1,
  input  Reset,
  input  CLK,
  input  IND0,
  input  IND1,
  input  IND2,
  output M0,
  output M1,
  output M2
);

  wire BACK, G0, G1, G2, get, Get0, Get1, Get2, neww0, neww1, neww2, NEXTT, Nind0, Nind1, Nind2, nop, Oind0,
       Oind1, Oind2, pop, Pop0, Pop1, Pop2, push, Push0, Push1, Push2;

  or or_1 (NEXTT, CLK, Reset);
  or or_2 (BACK, Reset, ~CLK);  // OR_Gate
  Commands commands_1 (.BIT0(Com0), .BIT1(Com1), .nop(nop), .push(push), .pop(pop), .get(get));
  TopOper topoper_1 (
    .RESET(Reset), .TOPoper0(Oind0), .TOPoper1(Oind1), .TOPoper2(Oind2), .Com0(Com0), .Com1(Com1),
    .NEWTOP0(neww0), .NEWTOP1(neww1), .NEWTOP3(neww2));
  SuperSubtract supersubtract_1 (
    .val0(IND0), .val1(IND1), .val2(IND2), .VALUE0(Nind0), .VAlUE1(Nind1), .VALUE2(Nind2), .D0(G0), .D1(G1),
    .D2(G2));
  and and_1 (Push0, push, Oind0);
  and and_2 (Push1, push, Oind1);
  and and_3 (Push2, push, Oind2);
  and and_4 (Pop0, pop, Nind0);
  and and_5 (Pop1, pop, Nind1);
  and and_6 (Pop2, pop, Nind2);
  and and_7 (Get0, get, G0);
  and and_8 (Get1, get, G1);
  and and_9 (Get2, get, G2);
  Dtrigger dtrigger_1 (.D(neww0), .CLK(NEXTT), .Q(Nind0));  // open: NQ
  Dtrigger dtrigger_2 (.D(neww1), .CLK(NEXTT), .Q(Nind1));  // open: NQ
  Dtrigger dtrigger_3 (.D(neww2), .CLK(NEXTT), .Q(Nind2));  // open: NQ
  Dtrigger dtrigger_4 (.D(Nind0), .CLK(BACK), .Q(Oind0));  // open: NQ
  Dtrigger dtrigger_5 (.D(Nind1), .CLK(BACK), .Q(Oind1));  // open: NQ
  Dtrigger dtrigger_6 (.D(Nind2), .CLK(BACK), .Q(Oind2));  // open: NQ
  or or_3 (M0, Push0, Pop0, Get0);
  or or_4 (M1, Push1, Pop1, Get1);
  or or_5 (M2, Push2, Pop2, Get2);
endmodule

module Commands (
  input  BIT0,
  input  BIT1,
  output nop,
  output push,
  output pop,
  output get
);

  and and_1 (nop, ~BIT0, ~BIT1);  // AND_Gate
  and and_2 (push, BIT0, ~BIT1);  // AND_Gate
  and and_3 (pop, ~BIT0, BIT1);  // AND_Gate
  and and_4 (get, BIT0, BIT1);

  // Other names for the same wires on the sheet: Command0 = BIT0; Command1 = BIT1
endmodule

module parser (
  input  FLAG,
  input  VAL0,
  input  VAL1,
  input  VAL2,
  input  VAL3,
  output out_6,
  output out_7,
  output out_8,
  output out_9
);

  bitParser bitparser_1 (.zatvor(FLAG), .istok(VAL0), .stok(out_6));
  bitParser bitparser_2 (.zatvor(FLAG), .istok(VAL1), .stok(out_7));
  bitParser bitparser_3 (.zatvor(FLAG), .istok(VAL2), .stok(out_8));
  bitParser bitparser_4 (.zatvor(FLAG), .istok(VAL3), .stok(out_9));
endmodule

module bitParser (
  input  zatvor,
  input  istok,
  output stok
);

  wire not_1_out;

  not not_1 (not_1_out, zatvor);
  // Transmission_Gate transmission_1: pin names not known; wires that end beside it: istok, not_1_out, zatvor, stok
endmodule

module RStrigger (
  input  R,
  input  S,
  output Q,
  output notQ
);

  wire nor_1_out, por_1_out;

  nor nor_1 (nor_1_out, Q, S);
  POR por_1 (.out(por_1_out));
  nor nor_2 (Q, R, notQ);
  or or_1 (notQ, nor_1_out, por_1_out);
endmodule

module Dtrigger (
  input  D,
  input  CLK,
  output Q,
  output NQ
);

  wire and_1_out, and_2_out;

  and and_1 (and_1_out, ~D, CLK);  // AND_Gate
  and and_2 (and_2_out, D, CLK);
  RStrigger rstrigger_1 (.R(and_1_out), .S(and_2_out), .Q(Q), .notQ(NQ));
endmodule

module MEM (
  input  Reset,
  input  CLK,
  input  VAL0,
  input  VAL1,
  input  VAL2,
  input  VAL3,
  input  Ind0,
  input  Ind1,
  input  Ind2,
  output O0,
  output O1,
  output O2,
  output O3
);

  wire blockofmemory_1_q0, blockofmemory_1_q1, blockofmemory_1_q2, blockofmemory_1_q3, blockofmemory_2_q0,
       blockofmemory_2_q1, blockofmemory_2_q2, blockofmemory_2_q3, blockofmemory_3_q0, blockofmemory_3_q1,
       blockofmemory_3_q2, blockofmemory_3_q3, blockofmemory_4_q0, blockofmemory_4_q1, blockofmemory_4_q2,
       blockofmemory_4_q3, blockofmemory_5_q0, blockofmemory_5_q1, blockofmemory_5_q2, blockofmemory_5_q3,
       F0, F1, F2, F3, F4, from3to5_1_val0, from3to5_1_val1, from3to5_1_val2, from3to5_1_val3,
       from3to5_1_val4;

  from3to5 from3to5_1 (
    .FIRSTBIN(Ind0), .SECONDBIN(Ind1), .THIRDBIN(Ind2), .VAL0(from3to5_1_val0), .VAL1(from3to5_1_val1),
    .VAL2(from3to5_1_val2), .VAL3(from3to5_1_val3), .VAL4(from3to5_1_val4));
  and and_1 (F0, from3to5_1_val0, CLK);
  and and_2 (F1, from3to5_1_val1, CLK);
  and and_3 (F2, from3to5_1_val2, CLK);
  and and_4 (F3, from3to5_1_val3, CLK);
  and and_5 (F4, from3to5_1_val4, CLK);
  BlockOfMemory blockofmemory_1 (
    .CLK(F0), .RESET(Reset), .VAL0(VAL0), .VAL1(VAL1), .VAL2(VAL2), .VAL3(VAL3), .Q0(blockofmemory_1_q0),
    .Q1(blockofmemory_1_q1), .Q2(blockofmemory_1_q2), .Q3(blockofmemory_1_q3));
  BlockOfMemory blockofmemory_2 (
    .CLK(F1), .RESET(Reset), .VAL0(VAL0), .VAL1(VAL1), .VAL2(VAL2), .VAL3(VAL3), .Q0(blockofmemory_2_q0),
    .Q1(blockofmemory_2_q1), .Q2(blockofmemory_2_q2), .Q3(blockofmemory_2_q3));
  BlockOfMemory blockofmemory_3 (
    .CLK(F2), .RESET(Reset), .VAL0(VAL0), .VAL1(VAL1), .VAL2(VAL2), .VAL3(VAL3), .Q0(blockofmemory_3_q0),
    .Q1(blockofmemory_3_q1), .Q2(blockofmemory_3_q2), .Q3(blockofmemory_3_q3));
  BlockOfMemory blockofmemory_4 (
    .CLK(F3), .RESET(Reset), .VAL0(VAL0), .VAL1(VAL1), .VAL2(VAL2), .VAL3(VAL3), .Q0(blockofmemory_4_q0),
    .Q1(blockofmemory_4_q1), .Q2(blockofmemory_4_q2), .Q3(blockofmemory_4_q3));
  BlockOfMemory blockofmemory_5 (
    .CLK(F4), .RESET(Reset), .VAL0(VAL0), .VAL1(VAL1), .VAL2(VAL2), .VAL3(VAL3), .Q0(blockofmemory_5_q0),
    .Q1(blockofmemory_5_q1), .Q2(blockofmemory_5_q2), .Q3(blockofmemory_5_q3));
  MUX mux_1 (
    .IND0(Ind0), .IND1(Ind1), .IND2(Ind2), .VAL00(blockofmemory_1_q0), .VAL01(blockofmemory_1_q1),
    .VAL02(blockofmemory_1_q2), .VAL03(blockofmemory_1_q3), .VAL10(blockofmemory_2_q0),
    .VAL11(blockofmemory_2_q1), .VAL12(blockofmemory_2_q2), .VAL13(blockofmemory_2_q3),
    .VAL20(blockofmemory_3_q0), .VAL21(blockofmemory_3_q1), .VAL22(blockofmemory_3_q2),
    .VAL23(blockofmemory_3_q3), .VAL30(blockofmemory_4_q0), .VAL31(blockofmemory_4_q1),
    .VAL32(blockofmemory_4_q2), .VAL33(blockofmemory_4_q3), .VAL40(blockofmemory_5_q0),
    .VAL41(blockofmemory_5_q1), .VAL42(blockofmemory_5_q2), .VAL43(blockofmemory_5_q3), .D0(O0), .D1(O1),
    .D2(O2), .D3(O3));
endmodule

module MUX (
  input  IND0,
  input  IND1,
  input  IND2,
  input  VAL00,
  input  VAL01,
  input  VAL02,
  input  VAL03,
  input  VAL10,
  input  VAL11,
  input  VAL12,
  input  VAL13,
  input  VAL20,
  input  VAL21,
  input  VAL22,
  input  VAL23,
  input  VAL30,
  input  VAL31,
  input  VAL32,
  input  VAL33,
  input  VAL40,
  input  VAL41,
  input  VAL42,
  input  VAL43,
  output D0,
  output D1,
  output D2,
  output D3
);

  wire D0_t, D1_t, D2_t, D3_t, D4, VAL00_t, VAL01_t, VAL02_t, VAL03_t, VAL10_t, VAL11_t, VAL12_t, VAL13_t,
       VAL20_t, VAL21_t, VAL22_t, VAL23_t, VAL30_t, VAL31_t, VAL32_t, VAL33_t, VAL40_t, VAL41_t, VAL42_t,
       VAL43_t;

  from3to5 from3to5_1 (
    .FIRSTBIN(IND0), .SECONDBIN(IND1), .THIRDBIN(IND2), .VAL0(D0_t), .VAL1(D1_t), .VAL2(D2_t), .VAL3(D3_t),
    .VAL4(D4));
  and and_1 (VAL00_t, VAL00, D0_t);
  and and_2 (VAL01_t, VAL01, D0_t);
  and and_3 (VAL02_t, VAL02, D0_t);
  and and_4 (VAL03_t, VAL03, D0_t);
  and and_5 (VAL10_t, VAL10, D1_t);
  and and_6 (VAL11_t, VAL11, D1_t);
  and and_7 (VAL12_t, VAL12, D1_t);
  and and_8 (VAL13_t, VAL13, D1_t);
  and and_9 (VAL20_t, VAL20, D2_t);
  and and_10 (VAL21_t, VAL21, D2_t);
  and and_11 (VAL22_t, VAL22, D2_t);
  and and_12 (VAL23_t, VAL23, D2_t);
  and and_13 (VAL30_t, VAL30, D3_t);
  and and_14 (VAL31_t, VAL31, D3_t);
  and and_15 (VAL32_t, VAL32, D3_t);
  and and_16 (VAL33_t, VAL33, D3_t);
  and and_17 (VAL40_t, VAL40, D4);
  and and_18 (VAL41_t, VAL41, D4);
  and and_19 (VAL42_t, VAL42, D4);
  and and_20 (VAL43_t, VAL43, D4);
  or or_1 (D0, VAL00_t, VAL10_t, VAL20_t, VAL30_t, VAL40_t);
  or or_2 (D1, VAL01_t, VAL11_t, VAL21_t, VAL31_t, VAL41_t);
  or or_3 (D2, VAL02_t, VAL12_t, VAL22_t, VAL32_t, VAL42_t);
  or or_4 (D3, VAL03_t, VAL13_t, VAL23_t, VAL33_t, VAL43_t);
endmodule

module BlockOfMemory (
  input  CLK,
  input  RESET,
  input  VAL0,
  input  VAL1,
  input  VAL2,
  input  VAL3,
  output Q0,
  output Q1,
  output Q2,
  output Q3
);

  wire and_1_out, and_2_out, and_3_out, and_4_out, CLK_t;

  or or_1 (CLK_t, RESET, CLK);
  and and_1 (and_1_out, VAL0, ~RESET);  // AND_Gate
  and and_2 (and_2_out, VAL1, ~RESET);  // AND_Gate
  and and_3 (and_3_out, VAL2, ~RESET);  // AND_Gate
  and and_4 (and_4_out, VAL3, ~RESET);  // AND_Gate
  Dtrigger dtrigger_1 (.D(and_1_out), .CLK(CLK_t), .Q(Q0));  // open: NQ
  Dtrigger dtrigger_2 (.D(and_2_out), .CLK(CLK_t), .Q(Q1));  // open: NQ
  Dtrigger dtrigger_3 (.D(and_3_out), .CLK(CLK_t), .Q(Q2));  // open: NQ
  Dtrigger dtrigger_4 (.D(and_4_out), .CLK(CLK_t), .Q(Q3));  // open: NQ

  // Other names for the same wires on the sheet: D0 = VAL0; D1 = VAL1; D2 = VAL2; D3 = VAL3
endmodule

module from3to5 (
  input  FIRSTBIN,
  input  SECONDBIN,
  input  THIRDBIN,
  output VAL0,
  output VAL1,
  output VAL2,
  output VAL3,
  output VAL4
);

  wire five, not_1_out, not_2_out, not_3_out, not_4_out, not_5_out, not_6_out, not_7_out, not_8_out,
       not_9_out, not_10_out, not_11_out, not_12_out, one, seven, six, two, zero;

  not not_1 (not_1_out, SECONDBIN);
  not not_2 (not_2_out, THIRDBIN);
  not not_3 (not_3_out, FIRSTBIN);
  not not_4 (not_4_out, THIRDBIN);
  not not_5 (not_5_out, THIRDBIN);
  not not_6 (not_6_out, FIRSTBIN);
  not not_7 (not_7_out, SECONDBIN);
  not not_8 (not_8_out, SECONDBIN);
  not not_9 (not_9_out, FIRSTBIN);
  not not_10 (not_10_out, FIRSTBIN);
  not not_11 (not_11_out, SECONDBIN);
  not not_12 (not_12_out, THIRDBIN);
  and and_1 (VAL3, FIRSTBIN, SECONDBIN, not_5_out);
  and and_2 (VAL4, not_6_out, not_7_out, THIRDBIN);
  and and_3 (five, FIRSTBIN, not_8_out, THIRDBIN);
  and and_4 (six, not_9_out, SECONDBIN, THIRDBIN);
  and and_5 (seven, FIRSTBIN, SECONDBIN, THIRDBIN);
  and and_6 (zero, not_10_out, not_11_out, not_12_out);
  and and_7 (one, FIRSTBIN, not_1_out, not_2_out);
  and and_8 (two, not_3_out, SECONDBIN, not_4_out);
  or or_1 (VAL0, zero, five);
  or or_2 (VAL1, one, six);
  or or_3 (VAL2, two, seven);

  // Other names for the same wires on the sheet: four = VAL4; I0 = FIRSTBIN; I1 = SECONDBIN; I2 = THIRDBIN;
  //   three = VAL3
endmodule

module from5to3 (
  input  val0,
  input  val1,
  input  val2,
  input  val3,
  input  val4,
  output binval0,
  output binval1,
  output binval2
);

  or or_1 (binval1, val2, val3);
  or or_2 (binval0, val1, val3);

  assign binval2 = val4;
endmodule

module substract (
  input  val0,
  input  val1,
  input  val2,
  output minusval0,
  output minusval1,
  output minusval2
);

  wire from3to5_1_val0, from3to5_1_val1, from3to5_1_val2, from3to5_1_val3, from3to5_1_val4;

  from3to5 from3to5_1 (
    .FIRSTBIN(val0), .SECONDBIN(val1), .THIRDBIN(val2), .VAL0(from3to5_1_val0), .VAL1(from3to5_1_val1),
    .VAL2(from3to5_1_val2), .VAL3(from3to5_1_val3), .VAL4(from3to5_1_val4));
  from5to3 from5to3_1 (
    .val0(from3to5_1_val1), .val1(from3to5_1_val2), .val2(from3to5_1_val3), .val3(from3to5_1_val4),
    .val4(from3to5_1_val0), .binval0(minusval0), .binval1(minusval1), .binval2(minusval2));
endmodule

module SuperSubtract (
  input  val0,
  input  val1,
  input  val2,
  input  VALUE0,
  input  VAlUE1,
  input  VALUE2,
  output D0,
  output D1,
  output D2
);

  wire and_1_out, and_2_out, and_3_out, and_4_out, and_5_out, and_6_out, and_7_out, and_8_out, and_9_out,
       and_10_out, and_11_out, and_12_out, and_13_out, and_14_out, and_15_out, NEWVALUE0, NEWVALUE1,
       NEWVALUE2, R0, R1, R2, R3, R4, substract_2_minusval0, substract_2_minusval1, substract_2_minusval2,
       VAL02, VAL03, VAL04, VAL12, VAL13, VAL14, VAL22, VAL23, VAL24;

  and and_1 (and_1_out, VALUE2, R0);
  and and_2 (and_2_out, substract_2_minusval2, R1);
  and and_3 (and_3_out, VAL22, R2);
  and and_4 (and_4_out, VAL23, R3);
  and and_5 (and_5_out, VAL24, R4);
  from3to5 from3to5_1 (
    .FIRSTBIN(val0), .SECONDBIN(val1), .THIRDBIN(val2), .VAL0(R0), .VAL1(R1), .VAL2(R2), .VAL3(R3), .VAL4(R4));
  or or_1 (NEWVALUE2, and_1_out, and_2_out, and_3_out, and_4_out, and_5_out);
  substract substract_1 (
    .val0(NEWVALUE0), .val1(NEWVALUE1), .val2(NEWVALUE2), .minusval0(D0), .minusval1(D1), .minusval2(D2));
  and and_6 (and_6_out, VAlUE1, R0);
  and and_7 (and_7_out, substract_2_minusval1, R1);
  and and_8 (and_8_out, VAL12, R2);
  and and_9 (and_9_out, VAL13, R3);
  and and_10 (and_10_out, VAL14, R4);
  or or_2 (NEWVALUE1, and_6_out, and_7_out, and_8_out, and_9_out, and_10_out);
  substract substract_2 (
    .val0(VALUE0), .val1(VAlUE1), .val2(VALUE2), .minusval0(substract_2_minusval0),
    .minusval1(substract_2_minusval1), .minusval2(substract_2_minusval2));
  and and_11 (and_11_out, VALUE0, R0);
  and and_12 (and_12_out, substract_2_minusval0, R1);
  and and_13 (and_13_out, VAL02, R2);
  and and_14 (and_14_out, VAL03, R3);
  and and_15 (and_15_out, VAL04, R4);
  or or_3 (NEWVALUE0, and_11_out, and_12_out, and_13_out, and_14_out, and_15_out);
  substract substract_3 (
    .val0(substract_2_minusval0), .val1(substract_2_minusval1), .val2(substract_2_minusval2),
    .minusval0(VAL02), .minusval1(VAL12), .minusval2(VAL22));
  substract substract_4 (
    .val0(VAL02), .val1(VAL12), .val2(VAL22), .minusval0(VAL03), .minusval1(VAL13), .minusval2(VAL23));
  substract substract_5 (
    .val0(VAL03), .val1(VAL13), .val2(VAL23), .minusval0(VAL04), .minusval1(VAL14), .minusval2(VAL24));

  // Other names for the same wires on the sheet: VAL00 = VALUE0; VAL10 = VAlUE1; VAL20 = VALUE2
endmodule

module add (
  input  val0,
  input  val1,
  input  val2,
  output plusval0,
  output plusval1,
  output plusval3
);

  wire from3to5_1_val0, from3to5_1_val1, from3to5_1_val2, from3to5_1_val3, from3to5_1_val4;

  from3to5 from3to5_1 (
    .FIRSTBIN(val0), .SECONDBIN(val1), .THIRDBIN(val2), .VAL0(from3to5_1_val0), .VAL1(from3to5_1_val1),
    .VAL2(from3to5_1_val2), .VAL3(from3to5_1_val3), .VAL4(from3to5_1_val4));
  from5to3 from5to3_1 (
    .val0(from3to5_1_val4), .val1(from3to5_1_val0), .val2(from3to5_1_val1), .val3(from3to5_1_val2),
    .val4(from3to5_1_val3), .binval0(plusval0), .binval1(plusval1), .binval2(plusval3));
endmodule

module TopOper (
  input  RESET,
  input  TOPoper0,
  input  TOPoper1,
  input  TOPoper2,
  input  Com0,
  input  Com1,
  output NEWTOP0,
  output NEWTOP1,
  output NEWTOP3
);

  wire and_3_out, and_4_out, and_5_out, and_6_out, and_7_out, and_8_out, and_9_out, and_10_out, and_11_out,
       isMin, isNone, isPlus, MINUSTOP0, MINUSTOP1, MINUSTOP2, or_1_out, or_2_out, or_3_out, PlusTop0,
       PlusTop1, PlusTop2;

  add add_1 (
    .val0(TOPoper0), .val1(TOPoper1), .val2(TOPoper2), .plusval0(PlusTop0), .plusval1(PlusTop1),
    .plusval3(PlusTop2));
  substract substract_1 (
    .val0(TOPoper0), .val1(TOPoper1), .val2(TOPoper2), .minusval0(MINUSTOP0), .minusval1(MINUSTOP1),
    .minusval2(MINUSTOP2));
  and and_1 (isMin, ~Com0, Com1);  // AND_Gate
  xnor xnor_1 (isNone, Com0, Com1);
  and and_2 (isPlus, Com0, ~Com1);  // AND_Gate
  and and_3 (and_3_out, isNone, TOPoper0);
  and and_4 (and_4_out, isPlus, PlusTop0);
  and and_5 (and_5_out, isMin, MINUSTOP0);
  and and_6 (and_6_out, isNone, TOPoper1);
  and and_7 (and_7_out, isPlus, PlusTop1);
  and and_8 (and_8_out, isMin, MINUSTOP1);
  and and_9 (and_9_out, isNone, TOPoper2);
  and and_10 (and_10_out, isPlus, PlusTop2);
  and and_11 (and_11_out, isMin, MINUSTOP2);
  or or_1 (or_1_out, and_3_out, and_4_out, and_5_out);
  or or_2 (or_2_out, and_6_out, and_7_out, and_8_out);
  or or_3 (or_3_out, and_9_out, and_10_out, and_11_out);
  and and_12 (NEWTOP0, or_1_out, ~RESET);  // AND_Gate
  and and_13 (NEWTOP1, or_2_out, ~RESET);  // AND_Gate
  and and_14 (NEWTOP3, or_3_out, ~RESET);  // AND_Gate

  // Other names for the same wires on the sheet: TOP0 = TOPoper0; TOP1 = TOPoper1; TOP2 = TOPoper2
endmodule
